# Fritzing sketch piezo_led_photoresistor (saved by Fritzing 0.3.19b)
breadboards: 1

parts:
  Arduino1 = Arduino
  J1 = Piezo Speaker
  R1 = Photocell (LDR) [package=THT]
  R2 = Resistor [resistance=220 package=THT]
  LED1 = RGB LED (6 legs) [package="5 mm [THT]"]
  R3 = Resistor [resistance=220 package=THT]
  R4 = Resistor [resistance=220 package=THT]

nets:
  N1: Arduino1.GND, J1.pin1, R2.Pin_1
  N2: Arduino1.D10, R4.Pin_0
  N3: Arduino1.D9, R3.Pin_0
  N4: Arduino1.D3, J1.pin2
  N5: Arduino1.+5V, R1.pin_0
  N6: Arduino1.A0, R1.pin_1, R2.Pin_0
  N7: LED1.Blue1, R3.Pin_1
  N8: LED1.Green, R4.Pin_1
